// Logisim project ALU.circ as structural Verilog
module main (
  input  OPCODE_0,
  input  OPCODE_1,
  input  OPCODE_2,
  input  ALT_OPCODE,
  input  INPUT0_0,
  input  INPUT1_0,
  input  INPUT0_1,
  input  INPUT1_1,
  input  INPUT0_2,
  input  INPUT1_2,
  input  INPUT0_3,
  input  INPUT1_3,
  output OUT0_0,
  output OUT0_1,
  output OUT0_2,
  output OUT0_3,
  output OUT1_0,
  output OUT1_1,
  output OUT1_2,
  output OUT1_3,
  output CARRY,
  output NEGATIVE,
  output OVERFLOW,
  output ZERO,
  output EQUAL,
  output LESS_OR_GREATER,
  output PARITY
);

  wire [7:0] and_1_out, and_2_out, bit_extender_1_out, demultiplexer_1_out0, not_1_out,
       operator_alternate_1_out0_0, operator_normal_1_out0_0;

  assign bit_extender_1_out = {{7{ALT_OPCODE}}, ALT_OPCODE};  // Bit_Extender bit_extender_1
  assign and_1_out = bit_extender_1_out & demultiplexer_1_out0;  // AND_Gate and_1, 8 bits wide
  Demultiplexer #(.select(3)) demultiplexer_1 (
    .out0(demultiplexer_1_out0[0]), .out1(demultiplexer_1_out0[1]), .out2(demultiplexer_1_out0[2]),
    .out3(demultiplexer_1_out0[3]), .out4(demultiplexer_1_out0[4]), .out5(demultiplexer_1_out0[5]),
    .out6(demultiplexer_1_out0[6]), .out7(demultiplexer_1_out0[7]), .in(1'b1),
    .sel({OPCODE_2, OPCODE_1, OPCODE_0}));
  assign not_1_out = ~bit_extender_1_out;  // NOT_Gate not_1, 8 bits wide
  assign and_2_out = demultiplexer_1_out0 & not_1_out;  // AND_Gate and_2, 8 bits wide
  operator_normal operator_normal_1 (
    .OP0(and_2_out[0]), .OP1(and_2_out[1]), .OP2(and_2_out[2]), .OP3(and_2_out[3]), .OP4(and_2_out[4]),
    .OP5(and_2_out[5]), .OP6(and_2_out[6]), .OP7(and_2_out[7]), .IN0_0(INPUT0_0), .IN1_0(INPUT1_0),
    .IN0_1(INPUT0_1), .IN1_1(INPUT1_1), .IN2_0(INPUT0_2), .IN2_1(INPUT1_2), .IN3_0(INPUT0_3),
    .IN3_1(INPUT1_3), .OUT0_0(operator_normal_1_out0_0[0]), .OUT0_1(operator_normal_1_out0_0[1]),
    .OUT0_2(operator_normal_1_out0_0[2]), .OUT0_3(operator_normal_1_out0_0[3]),
    .OUT1_0(operator_normal_1_out0_0[4]), .OUT1_1(operator_normal_1_out0_0[5]),
    .OUT1_2(operator_normal_1_out0_0[6]), .OUT1_3(operator_normal_1_out0_0[7]));  // open: CARRY, OVERFLOW, ZERO, EQUAL, LESS_OR_GREATER, PARITY
  operator_alternate operator_alternate_1 (
    .OP0(and_1_out[0]), .OP1(and_1_out[1]), .OP2(and_1_out[2]), .OP3(and_1_out[3]), .OP4(and_1_out[4]),
    .OP5(and_1_out[5]), .OP6(and_1_out[6]), .OP7(and_1_out[7]), .IN0_0(INPUT0_0), .IN1_0(INPUT1_0),
    .IN0_1(INPUT0_1), .IN1_1(INPUT1_1), .IN2_0(INPUT0_2), .IN2_1(INPUT1_2), .IN3_0(INPUT0_3),
    .IN3_1(INPUT1_3), .OUT0_0(operator_alternate_1_out0_0[0]), .OUT0_1(operator_alternate_1_out0_0[1]),
    .OUT0_2(operator_alternate_1_out0_0[2]), .OUT0_3(operator_alternate_1_out0_0[3]),
    .OUT1_0(operator_alternate_1_out0_0[4]), .OUT1_1(operator_alternate_1_out0_0[5]),
    .OUT1_2(operator_alternate_1_out0_0[6]), .OUT1_3(operator_alternate_1_out0_0[7]));  // open: CARRY
  assign {OUT1_3, OUT1_2, OUT1_1, OUT1_0, OUT0_3, OUT0_2, OUT0_1, OUT0_0} = operator_normal_1_out0_0;  // OR_Gate or_1, 8 bits wide OR_Gate

  // Notes on the sheet:
  //   DMX gets 3 bit input
  //   these gates are diodes
endmodule

module half_adder (
  input  INPUT_0,
  input  INPUT_1,
  output SUM,
  output CARRY
);

  xor xor_1 (SUM, INPUT_0, INPUT_1);
  and and_1 (CARRY, INPUT_0, INPUT_1);
endmodule

module full_adder_1_bit (
  input  INPUT_0,
  input  INPUT_1,
  input  CARRY_IN,
  output SUM,
  output CARRY_OUT
);

  wire half_adder_1_carry, half_adder_1_sum, half_adder_2_carry;

  half_adder half_adder_1 (.INPUT_0(INPUT_0), .INPUT_1(INPUT_1), .SUM(half_adder_1_sum), .CARRY(half_adder_1_carry));
  half_adder half_adder_2 (.INPUT_0(half_adder_1_sum), .INPUT_1(CARRY_IN), .SUM(SUM), .CARRY(half_adder_2_carry));
  or or_1 (CARRY_OUT, half_adder_2_carry, half_adder_1_carry);
endmodule

module adder_4_bit (
  input  INPUT0_0,
  input  INPUT1_0,
  input  INPUT0_1,
  input  INPUT1_1,
  input  INPUT0_2,
  input  INPUT1_2,
  input  INPUT0_3,
  input  INPUT1_3,
  output OUT_0,
  output OUT_1,
  output OUT_2,
  output OUT_3,
  output CARRY
);

  wire full_adder_1_bit_1_carry_out, full_adder_1_bit_2_carry_out, full_adder_1_bit_3_carry_out;

  full_adder_1_bit full_adder_1_bit_1 (
    .INPUT_0(INPUT0_0), .INPUT_1(INPUT1_0), .SUM(OUT_0), .CARRY_OUT(full_adder_1_bit_1_carry_out));  // open: CARRY_IN
  full_adder_1_bit full_adder_1_bit_2 (
    .INPUT_0(INPUT0_1), .INPUT_1(INPUT1_1), .CARRY_IN(full_adder_1_bit_1_carry_out), .SUM(OUT_1),
    .CARRY_OUT(full_adder_1_bit_2_carry_out));
  full_adder_1_bit full_adder_1_bit_3 (
    .INPUT_0(INPUT0_2), .INPUT_1(INPUT1_2), .CARRY_IN(full_adder_1_bit_2_carry_out), .SUM(OUT_2),
    .CARRY_OUT(full_adder_1_bit_3_carry_out));
  full_adder_1_bit full_adder_1_bit_4 (
    .INPUT_0(INPUT0_3), .INPUT_1(INPUT1_3), .CARRY_IN(full_adder_1_bit_3_carry_out), .SUM(OUT_3),
    .CARRY_OUT(CARRY));
endmodule

module operator_normal (
  input  OP0,
  input  OP1,
  input  OP2,
  input  OP3,
  input  OP4,
  input  OP5,
  input  OP6,
  input  OP7,
  input  IN0_0,
  input  IN1_0,
  input  IN0_1,
  input  IN1_1,
  input  IN2_0,
  input  IN2_1,
  input  IN3_0,
  input  IN3_1,
  output OUT0_0,
  output OUT0_1,
  output OUT0_2,
  output OUT0_3,
  output OUT1_0,
  output OUT1_1,
  output OUT1_2,
  output OUT1_3,
  output CARRY,
  output OVERFLOW,
  output ZERO,
  output EQUAL,
  output LESS_OR_GREATER,
  output PARITY
);

  wire ADD_SUB_to_CARRY, ADD_SUB_to_ZERO, MUL_to_CARRY, MUL_to_ZERO, nor_1_out, nor_2_out, or_1_out;
  wire [3:0] ADD_SUB_to_OUT0, MUL_to_OUT0;
  wire [7:0] and_1_out, and_2_out, bit_extender_1_out, bit_extender_2_out;

  or or_1 (or_1_out, OP0, OP1);
  assign bit_extender_1_out = {{7{or_1_out}}, or_1_out};  // Bit_Extender bit_extender_1
  assign bit_extender_2_out = {{7{OP2}}, OP2};  // Bit_Extender bit_extender_2
  assign and_1_out = bit_extender_1_out & {IN3_1, IN3_0, IN2_1, IN2_0, IN1_1, IN0_1, IN1_0, IN0_0};  // AND_Gate and_1, 8 bits wide
  assign and_2_out = bit_extender_2_out & {IN3_1, IN3_0, IN2_1, IN2_0, IN1_1, IN0_1, IN1_0, IN0_0};  // AND_Gate and_2, 8 bits wide
  adder_subber_4_bit adder_subber_4_bit_1 (
    .MODE(OP1), .INPUT0_0(and_1_out[0]), .INPUT1_0(and_1_out[1]), .INPUT0_1(and_1_out[2]),
    .INPUT1_1(and_1_out[3]), .INPUT0_2(and_1_out[4]), .INPUT1_2(and_1_out[5]), .INPUT0_3(and_1_out[6]),
    .INPUT1_3(and_1_out[7]), .OUT_0(ADD_SUB_to_OUT0[0]), .OUT_1(ADD_SUB_to_OUT0[1]),
    .OUT_2(ADD_SUB_to_OUT0[2]), .OUT_3(ADD_SUB_to_OUT0[3]), .CARRY(ADD_SUB_to_CARRY));
  multiplier_4_bit multiplier_4_bit_1 (
    .IN0_0(and_2_out[0]), .IN0_1(and_2_out[1]), .IN0_2(and_2_out[2]), .IN0_3(and_2_out[3]),
    .IN1_0(and_2_out[4]), .IN1_1(and_2_out[5]), .IN1_2(and_2_out[6]), .IN1_3(and_2_out[7]),
    .OUT0(MUL_to_OUT0[0]), .OUT1(MUL_to_OUT0[1]), .OUT2(MUL_to_OUT0[2]), .OUT3(MUL_to_OUT0[3]),
    .OUT4(OUT1_0), .OUT5(OUT1_1), .OUT6(OUT1_2), .OUT7(OUT1_3));
  assign {OUT1_3, OUT1_2, OUT1_1, OUT1_0} = {{3{1'b0}}, ADD_SUB_to_CARRY};  // Bit_Extender bit_extender_3
  nor nor_1 (nor_1_out, ADD_SUB_to_CARRY, ADD_SUB_to_OUT0[3], ADD_SUB_to_OUT0[2], ADD_SUB_to_OUT0[1], ADD_SUB_to_OUT0[0]);
  nor nor_2 (nor_2_out, OUT1_3, OUT1_2, OUT1_1, OUT1_0, MUL_to_OUT0[3], MUL_to_OUT0[2], MUL_to_OUT0[1], MUL_to_OUT0[0]);
  nor nor_3 (ADD_SUB_to_ZERO, or_1_out, nor_1_out);
  nor nor_4 (MUL_to_ZERO, OP2, nor_2_out);
  or or_2 (MUL_to_CARRY, OUT1_0, OUT1_1, OUT1_2, OUT1_3);
  assign {OUT0_3, OUT0_2, OUT0_1, OUT0_0} = ADD_SUB_to_OUT0 | MUL_to_OUT0;  // OR_Gate or_3, 4 bits wide
  or or_4 (CARRY, ADD_SUB_to_CARRY, MUL_to_CARRY);
  or or_5 (ZERO, ADD_SUB_to_ZERO, MUL_to_ZERO);
  or or_6 (PARITY, ADD_SUB_to_OUT0[0], MUL_to_OUT0[0]);

  // Other names for the same wires on the sheet: ADD_SUB_to_PARITY = ADD_SUB_to_OUT0[0];
  //   ADD_SUB_to_OUT1[3:0] = {OUT1_3, OUT1_2, OUT1_1, OUT1_0}; CMP_to_EQUAL = EQUAL;
  //   CMP_to_LESS_OR_GREATER = LESS_OR_GREATER; MUL_to_PARITY = MUL_to_OUT0[0]; to_AND = OP5; to_CMP = OP4;
  //   to_DIV = OP3; to_MUL = OP2; to_OR = OP6; to_OVERFLOW = OVERFLOW; to_XOR = OP7

  // Notes on the sheet:
  //   OPx = Input from opcode DMX
endmodule

module operator_alternate (
  input  OP0,
  input  OP1,
  input  OP2,
  input  OP3,
  input  OP4,
  input  OP5,
  input  OP6,
  input  OP7,
  input  IN0_0,
  input  IN1_0,
  input  IN0_1,
  input  IN1_1,
  input  IN2_0,
  input  IN2_1,
  input  IN3_0,
  input  IN3_1,
  output OUT0_0,
  output OUT0_1,
  output OUT0_2,
  output OUT0_3,
  output OUT1_0,
  output OUT1_1,
  output OUT1_2,
  output OUT1_3,
  output CARRY
);

  wire [7:0] and_1_out, bit_extender_1_out;

  assign bit_extender_1_out = {{7{OP0}}, OP0};  // Bit_Extender bit_extender_1
  assign and_1_out = bit_extender_1_out & {IN3_1, IN3_0, IN2_1, IN2_0, IN1_1, IN0_1, IN1_0, IN0_0};  // AND_Gate and_1, 8 bits wide
  adder_4_bit adder_4_bit_1 (
    .INPUT0_0(and_1_out[0]), .INPUT1_0(and_1_out[1]), .INPUT0_1(and_1_out[2]), .INPUT1_1(and_1_out[3]),
    .INPUT0_2(and_1_out[4]), .INPUT1_2(and_1_out[5]), .INPUT0_3(and_1_out[6]), .INPUT1_3(and_1_out[7]));  // open: OUT_0, OUT_1, OUT_2, OUT_3, CARRY

  // Other names for the same wires on the sheet: to_sub = OP1

  // Notes on the sheet:
  //   OPx = Input from opcode DMX
endmodule

module adder_4_bit_signed (
  input  INPUT0_0,
  input  INPUT1_0,
  input  INPUT0_1,
  input  INPUT1_1,
  input  INPUT0_2,
  input  INPUT1_2,
  input  SIGN0,
  input  SIGN1
);
endmodule

module half_subber (
  input  IN0,
  input  IN1,
  output OUT0,
  output BORROW
);

  wire not_1_out;

  not not_1 (not_1_out, IN0);
  xor xor_1 (OUT0, IN0, IN1);
  and and_1 (BORROW, not_1_out, IN1);
endmodule

module full_subber (
  input  IN0,
  input  IN1,
  input  IN_BORROW,
  output OUT0,
  output BORROW
);

  wire half_subber_1_borrow, half_subber_1_out0, half_subber_2_borrow;

  half_subber half_subber_1 (.IN0(IN0), .IN1(IN1), .OUT0(half_subber_1_out0), .BORROW(half_subber_1_borrow));
  half_subber half_subber_2 (.IN0(half_subber_1_out0), .IN1(IN_BORROW), .OUT0(OUT0), .BORROW(half_subber_2_borrow));
  or or_1 (BORROW, half_subber_2_borrow, half_subber_1_borrow);
endmodule

module subber_4_bit (
  input  IN0_0,
  input  IN1_0,
  input  IN0_1,
  input  IN1_1,
  input  IN0_2,
  input  IN1_2,
  input  IN0_3,
  input  IN1_3,
  output OUT_0,
  output OUT_1,
  output OUT_2,
  output OUT_3,
  output BORROW
);

  wire full_subber_1_borrow, full_subber_2_borrow, full_subber_3_borrow;

  full_subber full_subber_1 (.IN0(IN0_0), .IN1(IN1_0), .OUT0(OUT_0), .BORROW(full_subber_1_borrow));  // open: IN_BORROW
  full_subber full_subber_2 (
    .IN0(IN0_1), .IN1(IN1_1), .IN_BORROW(full_subber_1_borrow), .OUT0(OUT_1), .BORROW(full_subber_2_borrow));
  full_subber full_subber_3 (
    .IN0(IN0_2), .IN1(IN1_2), .IN_BORROW(full_subber_2_borrow), .OUT0(OUT_2), .BORROW(full_subber_3_borrow));
  full_subber full_subber_4 (.IN0(IN0_3), .IN1(IN1_3), .IN_BORROW(full_subber_3_borrow), .OUT0(OUT_3), .BORROW(BORROW));
endmodule

module adder_subber_4_bit (
  input  MODE,
  input  INPUT0_0,
  input  INPUT1_0,
  input  INPUT0_1,
  input  INPUT1_1,
  input  INPUT0_2,
  input  INPUT1_2,
  input  INPUT0_3,
  input  INPUT1_3,
  output OUT_0,
  output OUT_1,
  output OUT_2,
  output OUT_3,
  output CARRY
);

  wire full_adder_1_bit_1_carry_out, full_adder_1_bit_2_carry_out, full_adder_1_bit_3_carry_out, xor_1_out,
       xor_2_out, xor_3_out, xor_4_out;

  xor xor_1 (xor_1_out, MODE, INPUT1_0);
  xor xor_2 (xor_2_out, MODE, INPUT1_1);
  xor xor_3 (xor_3_out, MODE, INPUT1_2);
  xor xor_4 (xor_4_out, MODE, INPUT1_3);
  full_adder_1_bit full_adder_1_bit_1 (
    .INPUT_0(INPUT0_0), .INPUT_1(xor_1_out), .SUM(OUT_0), .CARRY_OUT(full_adder_1_bit_1_carry_out));  // open: CARRY_IN
  full_adder_1_bit full_adder_1_bit_2 (
    .INPUT_0(INPUT0_1), .INPUT_1(xor_2_out), .CARRY_IN(full_adder_1_bit_1_carry_out), .SUM(OUT_1),
    .CARRY_OUT(full_adder_1_bit_2_carry_out));
  full_adder_1_bit full_adder_1_bit_3 (
    .INPUT_0(INPUT0_2), .INPUT_1(xor_3_out), .CARRY_IN(full_adder_1_bit_2_carry_out), .SUM(OUT_2),
    .CARRY_OUT(full_adder_1_bit_3_carry_out));
  full_adder_1_bit full_adder_1_bit_4 (
    .INPUT_0(INPUT0_3), .INPUT_1(xor_4_out), .CARRY_IN(full_adder_1_bit_3_carry_out), .SUM(OUT_3),
    .CARRY_OUT(CARRY));
endmodule

module multiplier_4_bit (
  input  IN0_0,
  input  IN0_1,
  input  IN0_2,
  input  IN0_3,
  input  IN1_0,
  input  IN1_1,
  input  IN1_2,
  input  IN1_3,
  output OUT0,
  output OUT1,
  output OUT2,
  output OUT3,
  output OUT4,
  output OUT5,
  output OUT6,
  output OUT7
);

  wire [3:0] adder_4_bit_1_out_1, adder_4_bit_2_out_1, and_2_out, and_3_out, and_4_out, bit_extender_1_out,
       bit_extender_2_out, bit_extender_3_out, bit_extender_4_out;
  wire [3:1] and_1_out;

  assign bit_extender_1_out = {{3{IN1_0}}, IN1_0};  // Bit_Extender bit_extender_1
  assign bit_extender_2_out = {{3{IN1_1}}, IN1_1};  // Bit_Extender bit_extender_2
  assign bit_extender_3_out = {{3{IN1_2}}, IN1_2};  // Bit_Extender bit_extender_3
  assign bit_extender_4_out = {{3{IN1_3}}, IN1_3};  // Bit_Extender bit_extender_4
  assign {and_1_out, OUT0} = {IN0_3, IN0_2, IN0_1, IN0_0} & bit_extender_1_out;  // AND_Gate and_1, 4 bits wide
  assign and_2_out = bit_extender_2_out & {IN0_3, IN0_2, IN0_1, IN0_0};  // AND_Gate and_2, 4 bits wide
  assign and_3_out = {IN0_3, IN0_2, IN0_1, IN0_0} & bit_extender_3_out;  // AND_Gate and_3, 4 bits wide
  assign and_4_out = bit_extender_4_out & {IN0_3, IN0_2, IN0_1, IN0_0};  // AND_Gate and_4, 4 bits wide
  adder_4_bit adder_4_bit_1 (
    .INPUT0_0(and_2_out[0]), .INPUT1_0(and_1_out[1]), .INPUT0_1(and_2_out[1]), .INPUT1_1(and_1_out[2]),
    .INPUT0_2(and_2_out[2]), .INPUT1_2(and_1_out[3]), .INPUT0_3(and_2_out[3]), .INPUT1_3(1'b0), .OUT_0(OUT1),
    .OUT_1(adder_4_bit_1_out_1[0]), .OUT_2(adder_4_bit_1_out_1[1]), .OUT_3(adder_4_bit_1_out_1[2]),
    .CARRY(adder_4_bit_1_out_1[3]));
  adder_4_bit adder_4_bit_2 (
    .INPUT0_0(and_3_out[0]), .INPUT1_0(adder_4_bit_1_out_1[0]), .INPUT0_1(and_3_out[1]),
    .INPUT1_1(adder_4_bit_1_out_1[1]), .INPUT0_2(and_3_out[2]), .INPUT1_2(adder_4_bit_1_out_1[2]),
    .INPUT0_3(and_3_out[3]), .INPUT1_3(adder_4_bit_1_out_1[3]), .OUT_0(OUT2), .OUT_1(adder_4_bit_2_out_1[0]),
    .OUT_2(adder_4_bit_2_out_1[1]), .OUT_3(adder_4_bit_2_out_1[2]), .CARRY(adder_4_bit_2_out_1[3]));
  adder_4_bit adder_4_bit_3 (
    .INPUT0_0(and_4_out[0]), .INPUT1_0(adder_4_bit_2_out_1[0]), .INPUT0_1(and_4_out[1]),
    .INPUT1_1(adder_4_bit_2_out_1[1]), .INPUT0_2(and_4_out[2]), .INPUT1_2(adder_4_bit_2_out_1[2]),
    .INPUT0_3(and_4_out[3]), .INPUT1_3(adder_4_bit_2_out_1[3]), .OUT_0(OUT3), .OUT_1(OUT4), .OUT_2(OUT5),
    .OUT_3(OUT6), .CARRY(OUT7));

  // Notes on the sheet:
  //   Multiplied number
  //   Number of multiplications
endmodule

module divider_4_bit (
  input  IN0_0,
  input  IN0_1,
  input  IN0_2,
  input  IN0_3,
  input  IN1_0,
  input  IN1_1,
  input  IN1_2,
  input  IN1_3
);

  wire [3:0] and_1_out, bit_extender_1_out, subber_4_bit_1_out_1;

  assign bit_extender_1_out = {{3{IN1_0}}, IN1_0};  // Bit_Extender bit_extender_1
  assign and_1_out = {IN0_3, IN0_2, IN0_1, IN0_0} & bit_extender_1_out;  // AND_Gate and_1, 4 bits wide
  subber_4_bit subber_4_bit_1 (
    .IN0_0(and_1_out[0]), .IN0_1(and_1_out[1]), .IN0_2(and_1_out[2]), .IN0_3(and_1_out[3]),
    .OUT_1(subber_4_bit_1_out_1[0]), .OUT_2(subber_4_bit_1_out_1[1]), .OUT_3(subber_4_bit_1_out_1[2]),
    .BORROW(subber_4_bit_1_out_1[3]));  // open: IN1_0, IN1_1, IN1_2, IN1_3, OUT_0
endmodule
